# Fritzing sketch blackbox (saved by Fritzing 0.6.4b)
breadboards: 1

parts:
  U1 = 3-Axis Accelerometer Breakout
  Arduino1 = Arduino
  Arduino_LiliyPad1 = Arduino LilyPad
  Componente1 = Bluetooth Mate Silver

nets:
  N1: U1.Y, Arduino1.D3
  N2: U1.X, Arduino1.D2
  GND: U1.GND, Arduino1.GND, Arduino_LiliyPad1.GND, Componente1.TX_5V
  VDD: U1.VDD, Arduino1.+5V, Arduino_LiliyPad1.POW, Componente1.RX_5V
  N3: Arduino1.D9, Arduino_LiliyPad1.D1
  N4: Arduino1.D8, Arduino_LiliyPad1.D0
  N5: Arduino1.D1TX, Componente1.CTS_5V
  N6: Arduino1.D0RX, Componente1.VCC
  N7: Componente1.RTS_5V, Componente1.GND
